# Fritzing sketch layout (saved by Fritzing 0.8.3b)
breadboards: 1

parts:
  Left_Nob = Adafruit Gear-Reduced Stepper Motor (small)
  Right_Nob = Adafruit Gear-Reduced Stepper Motor (small)
  part = Arduino Uno (Rev3)
  part_2 = ULN2803A [package=THT]

nets:
  N1: Left_Nob.RED, Right_Nob.RED, part_2.0V
  N2: Left_Nob.ORANGE, part_2.Out_4
  N3: Left_Nob.YELLOW, part_2.Out_3
  N4: Left_Nob.PINK, part_2.Out_2
  N5: Left_Nob.BLUE, part_2.Out_1
  N6: Right_Nob.ORANGE, part_2.Out_8
  N7: Right_Nob.YELLOW, part_2.Out_7
  N8: Right_Nob.PINK, part_2.Out_6
  N9: Right_Nob.BLUE, part_2.Out_5
  N10: part.GND, part_2.COM_-_Common
  N11: part.D8, part_2.In_4
  N12: part.D9_PWM, part_2.In_3
  N13: part.D10_PWM/SS, part_2.In_2
  N14: part.D11_PWM/MOSI, part_2.In_1
  N15: part.D4, part_2.In_8
  N16: part.D5_PWM, part_2.In_7
  N17: part.D6_PWM, part_2.In_6
  N18: part.D7, part_2.In_5

custom parts:
  Adafruit Gear-Reduced Stepper Motor (small): Adafruit gear-reduction stepper motor (small)
